// Logisim project MiniMIPS.circ as structural Verilog
module InstructionFetch (
  input  [31:0] PC,
  output [31:0] OP,
  output [31:0] NewPC
);

  // Incrementer #(.width(30)) incrementer_1: pin names not known
  // MIPSProgramROM mipsprogramrom_1: pin names not known; wires that end beside it: PC, OP

  assign NewPC[1:0] = PC[1:0];
endmodule
